// Logisim project proccessor.circ as structural Verilog: 9 circuits, main circuit main
module main (
);

  FULL_ADDER_4BIT full_adder_4bit_1 ();  // open: CARRY_IN, A, A_1, A_2, A_3, B, B_1, B_2, B_3, Y, Y_1, Y_2, Y_3, CARRY_OUT
endmodule

module HALF_ADDER (
  input  A,
  input  B,
  output SUM,
  output CARRY
);

  xor xor_1 (SUM, A, B);
  and and_1 (CARRY, A, B);
endmodule

module INC_4BIT (
  input  A,
  input  A_1,
  input  A_2,
  input  A_3,
  input  INC,
  output Y,
  output Y_1,
  output Y_2,
  output Y_3,
  output CARRY
);

  wire half_adder_1_carry, half_adder_2_carry, half_adder_3_carry;

  HALF_ADDER half_adder_1 (.A(INC), .B(A), .SUM(Y), .CARRY(half_adder_1_carry));
  HALF_ADDER half_adder_2 (.A(half_adder_1_carry), .B(A_1), .SUM(Y_1), .CARRY(half_adder_2_carry));
  HALF_ADDER half_adder_3 (.A(half_adder_2_carry), .B(A_2), .SUM(Y_2), .CARRY(half_adder_3_carry));
  HALF_ADDER half_adder_4 (.A(half_adder_3_carry), .B(A_3), .SUM(Y_3), .CARRY(CARRY));
endmodule

module tows_comp (
  input  A,
  input  A_1,
  input  A_2,
  input  A_3,
  output Y,
  output Y_1,
  output Y_2,
  output Y_3,
  output CARRY
);

  wire not_1_out, not_2_out, not_3_out, not_4_out;

  not not_1 (not_1_out, A);
  not not_2 (not_2_out, A_1);
  not not_3 (not_3_out, A_2);
  not not_4 (not_4_out, A_3);
  INC_4BIT inc_4bit_1 (
    .A(not_1_out), .A_1(not_2_out), .A_2(not_3_out), .A_3(not_4_out), .INC(1'b1), .Y(Y), .Y_1(Y_1),
    .Y_2(Y_2), .Y_3(Y_3), .CARRY(CARRY));
endmodule

module FULL_ADDER_1BIT (
  input  CARRY_IN,
  input  B,
  input  A,
  output SUM,
  output CARRY_OUT
);

  wire or_1_out, or_2_out, or_3_out;

  or or_1 (or_1_out, A, B);
  or or_2 (or_2_out, A, CARRY_IN);
  or or_3 (or_3_out, B, CARRY_IN);
  xor xor_1 (SUM, CARRY_IN, B, A);
  and and_1 (CARRY_OUT, or_1_out, or_2_out, or_3_out);
endmodule

module FULL_ADDER_4BIT (
  input  CARRY_IN,
  input  A,
  input  A_1,
  input  A_2,
  input  A_3,
  input  B,
  input  B_1,
  input  B_2,
  input  B_3,
  output Y,
  output Y_1,
  output Y_2,
  output Y_3,
  output CARRY_OUT
);

  wire full_adder_1bit_1_carry_out, full_adder_1bit_2_carry_out, full_adder_1bit_3_carry_out;

  FULL_ADDER_1BIT full_adder_1bit_1 (
    .CARRY_IN(CARRY_IN), .B(B), .A(A), .SUM(Y), .CARRY_OUT(full_adder_1bit_1_carry_out));
  FULL_ADDER_1BIT full_adder_1bit_2 (
    .CARRY_IN(full_adder_1bit_1_carry_out), .B(B_1), .A(A_1), .SUM(Y_1),
    .CARRY_OUT(full_adder_1bit_2_carry_out));
  FULL_ADDER_1BIT full_adder_1bit_3 (
    .CARRY_IN(full_adder_1bit_2_carry_out), .B(B_2), .A(A_2), .SUM(Y_2),
    .CARRY_OUT(full_adder_1bit_3_carry_out));
  FULL_ADDER_1BIT full_adder_1bit_4 (
    .CARRY_IN(full_adder_1bit_3_carry_out), .B(B_3), .A(A_3), .SUM(Y_3), .CARRY_OUT(CARRY_OUT));
endmodule

module MUX_1BIT (
  input  A,
  input  B,
  input  A_notB,
  output Y
);

  wire and_1_out, and_2_out, not_1_out;

  not not_1 (not_1_out, A_notB);
  and and_1 (and_1_out, A, A_notB);
  and and_2 (and_2_out, not_1_out, B);
  or or_1 (Y, and_1_out, and_2_out);
endmodule

module MUX_4BIT (
  input  A,
  input  A_1,
  input  A_2,
  input  A_3,
  input  B,
  input  B_1,
  input  B_2,
  input  B_3,
  input  A_notB,
  output Y,
  output Y_1,
  output Y_2,
  output Y_3
);

  MUX_1BIT mux_1bit_1 (.A(A), .B(B), .A_notB(A_notB), .Y(Y));
  MUX_1BIT mux_1bit_2 (.A(A_1), .B(B_1), .A_notB(A_notB), .Y(Y_1));
  MUX_1BIT mux_1bit_3 (.A(A_2), .B(B_2), .A_notB(A_notB), .Y(Y_2));
  MUX_1BIT mux_1bit_4 (.A(A_3), .B(B_3), .A_notB(A_notB), .Y(Y_3));
endmodule

module DECODER1_2 (
  input  in_1,
  input  in_2,
  output out_3,
  output out_4
);

  wire not_1_out;

  not not_1 (not_1_out, in_1);
  and and_1 (out_3, not_1_out, in_2);
  and and_2 (out_4, in_1, in_2);
endmodule
